# Fritzing sketch pcb_comparator_v1 (saved by Fritzing 0.9.3b)
circuit board: 4.5699cm x 3.15595cm
breadboards: 1

parts:
  IC1 = IC, DIP package, 14 pins [chip_label=IC]
  J1 = female pin header, 3 pins [form="♀ (female)"]
  J38 = female pin header, 4 pins [form="♀ (female)"]
  J39 = female pin header, 4 pins [form="♀ (female)"]
  J40 = female pin header, 3 pins [form="♀ (female)"]
  J41 = female pin header, 3 pins [form="♀ (female)"]
  J42 = female pin header, 3 pins [form="♀ (female)"]
  LED3 = LED - 3mm [color="Red (633nm)" package="3 mm [THT]"]
  D1 = Rectifier Diode [package="Melf DO-213 AA [SMD]"]
  D2 = Rectifier Diode [package="Melf DO-213 AA [SMD]"]
  D3 = Rectifier Diode [package="Melf DO-213 AA [SMD]"]
  D4 = Rectifier Diode [package="Melf DO-213 AA [SMD]"]
  R1 = Resistor [tolerance=±5% resistance=470 package="1206 [SMD]"]
  R2 = Resistor [tolerance=±5% resistance=470 package="1206 [SMD]"]
  LED1 = LED - 3mm [color="Red (633nm)" package="3 mm [THT]"]
  J43 = female pin header, 1 pin [form="♀ (female)"]
  J44 = female pin header, 1 pin [form="♀ (female)"]
  J45 = female pin header, 3 pins [form="♀ (female)"]
  J46 = female pin header, 3 pins [form="♀ (female)"]
  J47 = female pin header, 1 pin [form="♀ (female)"]
  J48 = female pin header, 1 pin [form="♀ (female)"]
  J49 = female pin header, 1 pin [form="♀ (female)"]
  J50 = female pin header, 1 pin [form="♀ (female)"]

nets:
  N1: IC1.pin1, D1.anode, LED1.anode
  N2: IC1.pin2, J1.pin2
  N3: IC1.pin3, J41.pin3
  N4: IC1.pin4, J1.pin3, J38.pin3, J38.pin4, J40.pin1, J41.pin2, J42.pin2, J45.pin3, J46.pin1
  N5: IC1.pin5, J49.pin1
  N6: IC1.pin6, J45.pin2
  N7: IC1.pin7, J47.pin1
  N8: IC1.pin8, J48.pin1
  N9: IC1.pin9, J46.pin2
  N10: IC1.pin10, J50.pin1
  N11: IC1.pin11, J39.pin1, J40.pin3, J46.pin3
  N12: IC1.pin12, J42.pin1
  N13: IC1.pin13, J40.pin2
  N14: IC1.pin14, LED3.anode, D3.anode
  N15: J1.pin1, J38.pin1, J38.pin2, J41.pin1, J42.pin3, R1.Pin_0, R2.Pin_1, J45.pin1
  N16: LED3.cathode, R2.Pin_0
  N17: D1.cathode, D2.anode
  N18: D2.cathode, J43.pin1
  N19: D3.cathode, D4.anode
  N20: D4.cathode, J44.pin1
  N21: R1.Pin_1, LED1.cathode
