# Fritzing sketch pcb_main_v4 (saved by Fritzing 0.9.3b)
circuit board: 12cm x 12cm
breadboards: 1

parts:
  U3 = LuaNode32 / ESP32
  IR_LED6 = LED - 5mm [color="Infrared (940nm)" package="5 mm [THT]"]
  LED7 = LED - 3mm [color="Red (633nm)" package="3 mm [THT]"]
  470R = Resistor [tolerance=±5% resistance=470 package="1206 [SMD]"]
  220R = Resistor [tolerance=±5% resistance=220 package="1206 [SMD]"]
  LED8 = LED - 3mm [color="Red (633nm)" package="3 mm [THT]"]
  IR_LED7 = LED - 5mm [color="Infrared (940nm)" package="5 mm [THT]"]
  220R_2 = Resistor [tolerance=±5% resistance=220 package="1206 [SMD]"]
  470R_2 = Resistor [tolerance=±5% resistance=470 package="1206 [SMD]"]
  LED9 = LED - 3mm [color="Red (633nm)" package="3 mm [THT]"]
  LED10 = LED - 3mm [color="Red (633nm)" package="3 mm [THT]"]
  IR_LED8 = LED - 5mm [color="Infrared (940nm)" package="5 mm [THT]"]
  IR_LED9 = LED - 5mm [color="Infrared (940nm)" package="5 mm [THT]"]
  470R_3 = Resistor [tolerance=±5% resistance=470 package="1206 [SMD]"]
  220R_3 = Resistor [tolerance=±5% resistance=220 package="1206 [SMD]"]
  470R_4 = Resistor [tolerance=±5% resistance=470 package="1206 [SMD]"]
  220R_4 = Resistor [tolerance=±5% resistance=220 package="1206 [SMD]"]
  TCS34725 = Generic female header - 7 pins [form="♀ (female)" package=THT]
  J60 = female pin header, 5 pins [form="♀ (female)"]
  J59 = female pin header, 5 pins [form="♀ (female)"]
  GY-511 = Generic female header - 8 pins [form="♀ (female)" package=THT]
  J63 = female pin header, 2 pins [form="♀ (female)"]
  ML = female pin header, 3 pins [form="♀ (female)"]
  MR = female pin header, 3 pins [form="♀ (female)"]
  LED_(S) = female pin header, 3 pins [form="♀ (female)"]
  1uF = Electrolytic Capacitor [capacitance=1µF package="100 mil [THT, electrolytic]"]
  1uF_2 = Electrolytic Capacitor [capacitance=1µF package="100 mil [THT, electrolytic]"]
  LM1117 = Voltage Regulator LM1117 [package=sot223]
  EnL = female pin header, 3 pins [form="♀ (female)"]
  EnR = female pin header, 3 pins [form="♀ (female)"]
  J71 = female pin header, 3 pins [form="♀ (female)"]
  J72 = female pin header, 2 pins [form="♀ (female)"]
  7404 = 7404 NOT [package="DIP (Dual Inline) [THT]"]
  J73 = female pin header, 4 pins [form="♀ (female)"]
  4k7 = Resistor [tolerance=±5% resistance=4.7k package="1206 [SMD]"]
  4k7_2 = Resistor [tolerance=±5% resistance=4.7k package="1206 [SMD]"]
  100uF = Electrolytic Capacitor [capacitance=0.47mF voltage=16V package="100 mil [THT, electrolytic]"]
  100uF_2 = Electrolytic Capacitor [capacitance=1µF package="100 mil [THT, electrolytic]"]
  J74 = Generic female header - 3 pins [form="♀ (female)" package=THT]
  J75 = Generic female header - 3 pins [form="♀ (female)" package=THT]
  J76 = female pin header, 4 pins [form="♀ (female)"]
  J77 = female pin header, 4 pins [form="♀ (female)"]
  J78 = Generic female header - 3 pins [form="♀ (female)" package=THT]
  J79 = Generic female header - 3 pins [form="♀ (female)" package=THT]
  (S)Prox = female pin header, 3 pins [form="♀ (female)"]
  Power_(S) = female pin header, 4 pins [form="♀ (female)"]
  SW1 = DIP SWITCH [package=dipswitch-02]
  J80 = female pin header, 1 pin [form="♀ (female)"]
  J81 = female pin header, 2 pins [form="♀ (female)"]
  J82 = female pin header, 2 pins [form="♀ (female)"]
  J83 = female pin header, 1 pin [form="♀ (female)"]
  J84 = female pin header, 3 pins [form="♀ (female)"]
  PCF_2 = PCF 8574 [chip_label="PCF 8574" package="DIP (Dual Inline) [THT]"]

nets:
  N1: U3.EN, J80.pin1
  N2: U3.VP, 7404.5Y
  N3: U3.VN, 7404.4Y
  N4: U3.D34, 7404.6Y
  N5: U3.D35, 1uF_2.+, Power_(S).pin1
  N6: U3.D32, 1uF.+, (S)Prox.pin3
  N7: U3.D33, 7404.1Y
  N8: U3.D25, 7404.2A, J73.pin1
  N9: U3.D26, 7404.3A, J73.pin3
  N10: U3.D27, J82.pin1
  N11: U3.D14, J82.pin2
  N12: U3.D12, ML.pin3
  N13: U3.D13, MR.pin3
  GND: U3.GND, IR_LED6.cathode, IR_LED7.cathode, IR_LED8.cathode, IR_LED9.cathode, TCS34725.GND, J60.pin1, GY-511.GND, ML.pin1, MR.pin1, LED_(S).pin3, 1uF.-, 1uF_2.-, LM1117.ADJ, EnL.pin3, EnR.pin3, J72.pin1, 7404.GND, 100uF.-, 100uF_2.-, J74.GND, J75.GND, J76.pin1, J76.pin2, J77.pin1, J78.GND, J79.GND, (S)Prox.pin1, Power_(S).pin2, SW1.1, SW1.2, J81.pin1, PCF_2.GND
  5V: U3.Vin, TCS34725.5V, J59.pin5, GY-511.5V, ML.pin2, MR.pin2, LED_(S).pin2, LM1117.IN, 4k7.Pin_0, 4k7_2.Pin_0, 100uF.+, J76.pin3, J76.pin4, Power_(S).pin3, PCF_2.A0, PCF_2.A1, PCF_2.A2, PCF_2.Vcc
  VCC: U3.3V3, 470R.Pin_1, 470R_2.Pin_0, 470R_3.Pin_1, 470R_4.Pin_0, LM1117.OUT, EnL.pin2, EnR.pin2, J72.pin2, 7404.Vcc, 100uF_2.+, J74.Vcc, J75.Vcc, J77.pin2, J78.Vcc, J79.Vcc, (S)Prox.pin2, J81.pin2
  N14: U3.D15, J71.pin1
  N15: U3.D2, J71.pin2
  N16: U3.D4, J71.pin3
  N17: U3.RX2, 220R.Pin_0, 220R_2.Pin_0, 220R_3.Pin_0, 220R_4.Pin_0
  N18: U3.TX2, EnR.pin1
  N19: U3.D5, EnL.pin1
  N20: U3.D18, SW1.4
  N21: U3.D19, SW1.3
  N22: U3.D21, TCS34725.SDA, GY-511.SDA, 4k7_2.Pin_1, J77.pin4, PCF_2.SDA
  N23: U3.RX0, J63.pin2
  N24: U3.TX0, J63.pin1
  N25: U3.D22, TCS34725.SCL, GY-511.SCL, 4k7.Pin_1, J77.pin3, PCF_2.SCL
  N26: U3.D23, LED_(S).pin1
  N27: IR_LED6.anode, 220R.Pin_1
  N28: LED7.cathode, 7404.6A, J78.Out
  N29: LED7.anode, 470R.Pin_0
  N30: LED8.cathode, 7404.5A, J79.Out
  N31: LED8.anode, 470R_2.Pin_1
  N32: IR_LED7.anode, 220R_2.Pin_1
  N33: LED9.cathode, 7404.4A, J74.Out
  N34: LED9.anode, 470R_3.Pin_0
  N35: LED10.cathode, 7404.1A, J75.Out
  N36: LED10.anode, 470R_4.Pin_1
  N37: IR_LED8.anode, 220R_4.Pin_1
  N38: IR_LED9.anode, 220R_3.Pin_1
  N39: TCS34725.LED, TCS34725.INT
  N40: J60.pin2, PCF_2.P3
  N41: J60.pin3, PCF_2.P2
  N42: J60.pin4, PCF_2.P1
  N43: J60.pin5, PCF_2.P0
  N44: J59.pin1, PCF_2.P4
  N45: J59.pin2, PCF_2.P5
  N46: J59.pin3, PCF_2.P6
  N47: J59.pin4, PCF_2.P7
  N48: GY-511.DRDY, J84.pin3
  N49: GY-511.INT1, J84.pin2
  N50: GY-511.INT2, J84.pin1
  N51: 7404.2Y, J73.pin2
  N52: 7404.3Y, J73.pin4
  N53: J83.pin1, PCF_2.~INT

notes:
  JLCJLCJLC

custom parts:
  LuaNode32 / ESP32: ESP32 based LuaNode32
  Generic female header - 7 pins: Generic female header
  Generic female header - 8 pins: Generic female header
  7404 NOT: Hex Inverter
  Generic female header - 3 pins: Generic female header
  PCF 8574: I2C Port Expander
