# Fritzing sketch pcb_motors_v1 (saved by Fritzing 0.9.3b)
circuit board: 2.25cm x 2.4cm
breadboards: 1

parts:
  J85 = female pin header, 4 pins [form="♀ (female)"]
  MR1 = female pin header, 3 pins [form="♀ (female)"]
  ML1 = female pin header, 3 pins [form="♀ (female)"]
  Part1 = Motor Driver 1A Dual TB6612FNG
  J86 = female pin header, 2 pins [form="♀ (female)"]
  J87 = female pin header, 2 pins [form="♀ (female)"]

nets:
  N1: J85.pin1, Part1.BIN2
  N2: J85.pin2, Part1.BIN1
  N3: J85.pin3, Part1.AIN1
  N4: J85.pin4, Part1.AIN2
  GND: MR1.pin1, ML1.pin1, Part1.GND
  5V: MR1.pin2, ML1.pin2, Part1.VCC, Part1.VM, Part1.STBY
  N5: MR1.pin3, Part1.PWMB
  N6: ML1.pin3, Part1.PWMA
  N7: Part1.B01, J87.pin1
  N8: Part1.B02, J87.pin2
  N9: Part1.A02, J86.pin1
  N10: Part1.A01, J86.pin2
