# Fritzing sketch pcb_power_v1 (saved by Fritzing 0.9.3b)
circuit board: 4.5cm x 4cm
breadboards: 1

parts:
  IN- = female pin header, 1 pin [form="♀ (female)"]
  IN+ = female pin header, 1 pin [form="♀ (female)"]
  VOut- = female pin header, 1 pin [form="♀ (female)"]
  VOut+ = female pin header, 1 pin [form="♀ (female)"]
  BAT+ = female pin header, 1 pin [form="♀ (female)"]
  BAT- = female pin header, 1 pin [form="♀ (female)"]
  J1 = female pin header, 3 pins [form="♀ (female)"]
  J2 = female pin header, 2 pins [form="♀ (female)"]
  J3 = female pin header, 2 pins [form="♀ (female)"]
  J5 = female pin header, 4 pins [form="♀ (female)"]
  D5 = Zener Diode [part_number=1N4732A breakdown_voltage=3.6V package="300 mil [THT]"]
  D1 = Rectifier Diode [package="Melf DO-213 AA [SMD]"]
  D4 = Rectifier Diode [package="Melf DO-213 AA [SMD]"]
  D6 = Rectifier Diode [package="Melf DO-213 AA [SMD]"]
  D7 = Rectifier Diode [package="Melf DO-213 AA [SMD]"]
  Act = female pin header, 1 pin [form="♀ (female)"]
  R1 = Resistor [tolerance=±5% resistance=4.7k package="1206 [SMD]"]
  R2 = Resistor [tolerance=±5% resistance=10k package="1206 [SMD]"]
  J6 = female pin header, 2 pins [form="♀ (female)"]

nets:
  N1: IN-.pin1, D1.anode, D7.anode
  N2: IN+.pin1, D4.cathode, D6.cathode
  N3: VOut-.pin1, J5.pin2
  N4: VOut+.pin1, J5.pin1
  N5: BAT+.pin1, J1.pin2, R1.Pin_0, J6.pin2
  GND: BAT-.pin1, J2.pin2, D5.cathode, R2.Pin_0, J6.pin1
  N6: J1.pin3, J2.pin1
  N7: J3.pin1, D1.cathode, D4.anode
  N8: J3.pin2, D6.anode, D7.cathode
  N9: J5.pin3, D5.anode, R1.Pin_1, R2.Pin_1
  N10: J5.pin4, Act.pin1

notes:
  - BOut +
  + BIn -
