# Fritzing sketch pcb_power_v2 (saved by Fritzing 0.9.3b)
circuit board: 6.8cm x 1.3cm
breadboards: 1

parts:
  10k = Resistor [tolerance=±5% resistance=10k package="1206 [SMD]"]
  SW1 = DIP SWITCH [package=dipswitch-02]
  J8 = female pin header, 2 pins [form="♀ (female)"]
  2k2 = Resistor [tolerance=±5% resistance=2.2k package="1206 [SMD]"]
  0_1uF = Ceramic Capacitor [capacitance=100nF package="1206 [SMD, multilayer]"]
  Buck_Conv = female pin header, 4 pins [form="♀ (female)"]
  Robot_In = female pin header, 3 pins [form="♀ (female)"]
  J11 = female pin header, 3 pins [form="♀ (female)"]
  J12 = female pin header, 3 pins [form="♀ (female)"]
  Battery = female pin header, 2 pins [form="♀ (female)"]
  D1 = Rectifier Diode [breakdown_voltage=3.6V package="Melf DO-213 AA [SMD]"]
  D2 = Rectifier Diode [breakdown_voltage=3.6V package="Melf DO-213 AA [SMD]"]
  D3 = Rectifier Diode [breakdown_voltage=3.6V package="Melf DO-213 AA [SMD]"]
  D4 = Rectifier Diode [breakdown_voltage=3.6V package="Melf DO-213 AA [SMD]"]
  Charger = female pin header, 2 pins [form="♀ (female)"]
  Buck_Conv1 = female pin header, 4 pins [form="♀ (female)"]

nets:
  8.4V: 10k.Pin_0, Buck_Conv.pin2, J12.pin2, Buck_Conv1.pin2
  Vmon: 10k.Pin_1, 2k2.Pin_0, 0_1uF.1, Robot_In.pin3
  N1: SW1.1, J8.pin2
  N2: SW1.2, J8.pin1
  GND: SW1.3, SW1.4, 2k2.Pin_1, 0_1uF.0, Buck_Conv.pin3, Robot_In.pin2, J11.pin2, Buck_Conv1.pin1, Buck_Conv1.pin3
  5V: Buck_Conv.pin4, Robot_In.pin1, Buck_Conv1.pin4
  N3: J11.pin1, D1.anode, D3.anode
  N4: J12.pin1, D2.cathode, D4.cathode
  N5: Battery.pin1, D3.cathode, D4.anode, Charger.pin1
  N6: Battery.pin2, D1.cathode, D2.anode, Charger.pin2

notes:
  Swarm Robotics, 2
